# Fritzing sketch cricket (saved by Fritzing 0.9.3b)
stripboards: 1

parts:
  DFPlayer_Mini1 = DFPlayer MINI [package="DIP (Dual Inline) [THT]"]
  Part1 = Arduino Nano (Rev3.0)
  Part2 = HC-SR501 Body Sensor Module
  R1 = Photocell (LDR) [package=THT]
  R2 = Resistor [tolerance=±5% resistance=10k package=THT]
  SP1 = SPEAKER [package=pcb_mount_speaker]
  R3 = Resistor [tolerance=±5% resistance=1k package=THT]
  Sensor1 = TTP223B Capacitive Touch Sensor Module

nets:
  VCC: DFPlayer_Mini1.VCC, Part1.5V, Part2.VCC, R1.pin_1, Sensor1.VCC
  N1: DFPlayer_Mini1.RX, R3.Pin_0
  N2: DFPlayer_Mini1.TX, Part1.D5
  N3: DFPlayer_Mini1.SPK1, SP1.-
  GND: DFPlayer_Mini1.GND, Part1.GND, Part2.GND, R2.Pin_0, Sensor1.GND
  N4: DFPlayer_Mini1.SPK2, SP1.+
  N5: Part1.D4, R3.Pin_1
  N6: Part1.D8, Part2.OUT
  N7: Part1.D9, Sensor1.SIG
  N8: Part1.A0, R1.pin_0, R2.Pin_1

custom parts:
  DFPlayer MINI: MP3 module by DFRobot.com for playing Music from an SD-Card. Supports WAV and MP3 files.
  HC-SR501 Body Sensor Module: Pyroelectric Infrared PIR Motion Sensor Detector Module
  TTP223B Capacitive Touch Sensor Module: The TTP223B capacitive touch sensor module uses the TTP223B IC. The appropriate voltage is approximately 2 to 5.5 volts.
